# Fritzing sketch weather-station (saved by Fritzing 0.9.2b)
breadboards: 1

parts:
  Arduino_Uno = Arduino Uno (Rev3)
  DHT22 = DHT22 Humidity and Temperature Sensor
  TSL2561 = Adafruit TSL2561 [part_number="Adafruit #439"]
  LED1 = LED - 5mm [color="Green (555nm)" package="5 mm [THT]"]
  R1 = Resistor [tolerance=±5% resistance=220 package=THT]
  BMP180 = Adafruit BMP180
  HC-06 = mystery part, 4 pins [chip_label=HC-06]

nets:
  N1: Arduino_Uno.A4/SDA, TSL2561.SDA, BMP180.SDA
  N2: Arduino_Uno.A5/SCL, TSL2561.SCL, BMP180.SCL
  N3: Arduino_Uno.D0/RX, HC-06.pin1
  N4: Arduino_Uno.D1/TX, HC-06.pin2
  N5: Arduino_Uno.D2, DHT22.DATA
  N6: Arduino_Uno.D4, R1.Pin_0
  3V3: Arduino_Uno.3V3, BMP180.+5V
  5V: Arduino_Uno.5V, DHT22.VDD, TSL2561.VIN, HC-06.pin4
  GND: Arduino_Uno.GND, DHT22.GND, TSL2561.GND, TSL2561.ADDR, LED1.cathode, BMP180.GND, HC-06.pin3
  N7: LED1.anode, R1.Pin_1

custom parts:
  Adafruit TSL2561: The TSL2561 luminosity sensor is an advanced digital light sensor, ideal for use in a wide range of light situations. Compared to low cost CdS cells, this sensor is more precise, allowing for exact lux calculations and can be configured for different gain/timing ranges to detect light ranges from up to 0.1 - 40,000+ Lux on the fly. The best part of this sensor is that it contains both infrared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
  Adafruit BMP180: This precision sensor from Bosch is the best low-cost sensing solution for measuring barometric pressure and temperature. Because pressure changes with altitude you can also use it as an altimeter! The sensor is soldered onto a PCB with a 3.3V regulator, I2C level shifter and pull-up resistors on the I2C pins. The BMP180 is the next-generation of sensors from Bosch, and replaces the BMP085.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
