# Fritzing sketch weather-station (saved by Fritzing 0.9.3b)
breadboards: 1

parts:
  DHT22 = DHT22 Humidity and Temperature Sensor
  TSL2561 = Adafruit TSL2561 [part_number="Adafruit #439"]
  BMP180 = Adafruit BMP180
  Adafruit_HUZZAH_ESP8266_Breakout1 = Adafruit HUZZAH ESP8266 Breakout [part_number=2471]
  U1 = LIPO-1000mAh [package=lipo-1000]
  R1 = Resistor [tolerance=±5% resistance=10k package="0603 [SMD]"]

nets:
  N1: DHT22.VDD, Adafruit_HUZZAH_ESP8266_Breakout1.#14
  N2: DHT22.DATA, Adafruit_HUZZAH_ESP8266_Breakout1.#12, R1.Pin_0
  GND: DHT22.GND, TSL2561.GND, TSL2561.ADDR, BMP180.GND, Adafruit_HUZZAH_ESP8266_Breakout1.GND, U1.-
  3.3V: TSL2561.3.3V, BMP180.+3V3, Adafruit_HUZZAH_ESP8266_Breakout1.3V, R1.Pin_1
  N3: TSL2561.SDA, BMP180.SDA, Adafruit_HUZZAH_ESP8266_Breakout1.#4
  N4: TSL2561.SCL, BMP180.SCL, Adafruit_HUZZAH_ESP8266_Breakout1.#5
  N5: Adafruit_HUZZAH_ESP8266_Breakout1.VBat, U1.+
  N6: Adafruit_HUZZAH_ESP8266_Breakout1.#16, Adafruit_HUZZAH_ESP8266_Breakout1.RST

custom parts:
  Adafruit TSL2561: The TSL2561 luminosity sensor is an advanced digital light sensor, ideal for use in a wide range of light situations. Compared to low cost CdS cells, this sensor is more precise, allowing for exact lux calculations and can be configured for different gain/timing ranges to detect light ranges from up to 0.1 - 40,000+ Lux on the fly. The best part of this sensor is that it contains both infrared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
  Adafruit BMP180: This precision sensor from Bosch is the best low-cost sensing solution for measuring barometric pressure and temperature. Because pressure changes with altitude you can also use it as an altimeter! The sensor is soldered onto a PCB with a 3.3V regulator, I2C level shifter and pull-up resistors on the I2C pins. The BMP180 is the next-generation of sensors from Bosch, and replaces the BMP085.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
